// Logisim project ALU.circ as structural Verilog: 13 circuits, main circuit main
module main (
  output halt,
  output [8:0] counter,
  output [3:0] op,
  output [15:0] a,
  output [15:0] b,
  output [15:0] oracle,
  output [15:0] result,
  output err_oracle,
  output error,
  output ok,
  output start_delimiter
);

  wire and_1_out, and_2_out, clock_1_out, comparator_1_eq, comparator_2_eq;

  Clock clock_1 (.out(clock_1_out));
  Counter #(.width(9), .max('h1ff), .trigger("falling")) counter_1 (
    .Q(counter), .carry(halt), .clk(clock_1_out));  // open: load, D, count, clr
  RAM #(.addrWidth(12), .dataWidth(4), .bus("separate")) ram_1 (
    .addr({counter, 3'b000}), .data(op), .ld(1'b1));  // open: din, str, sel, clk, clr
  RAM #(.addrWidth(12), .dataWidth(16), .bus("separate")) ram_2 (
    .addr({counter, 3'b001}), .data(a), .ld(1'b1));  // open: din, str, sel, clk, clr
  RAM #(.addrWidth(12), .dataWidth(16), .bus("separate")) ram_3 (
    .addr({counter, 3'b010}), .data(b), .ld(1'b1));  // open: din, str, sel, clk, clr
  RAM #(.addrWidth(12), .dataWidth(16), .bus("separate")) ram_4 (
    .addr({counter, 3'b011}), .data(oracle), .ld(1'b1));  // open: din, str, sel, clk, clr
  RAM #(.addrWidth(12), .dataWidth(1), .bus("separate")) ram_5 (
    .addr({counter, 3'b100}), .data(err_oracle), .ld(1'b1));  // open: din, str, sel, clk, clr
  RAM #(.addrWidth(12), .dataWidth(1), .bus("separate")) ram_6 (
    .addr({counter, 3'b101}), .data(start_delimiter), .ld(1'b1));  // open: din, str, sel, clk, clr
  _16_bit_ALU u_16_bit_alu_1 (.ALU_code(op), .a(a), .b(b), .overflow(error), .result(result));
  Comparator #(.width(1), .mode("unsigned")) comparator_1 (
    .a(error), .b(err_oracle), .eq(comparator_1_eq));  // open: gt, lt
  Comparator #(.width(16)) comparator_2 (.a(result), .b(oracle), .eq(comparator_2_eq));  // open: gt, lt
  and and_1 (and_1_out, comparator_1_eq, error);
  and and_2 (and_2_out, comparator_2_eq, comparator_1_eq, ~error);  // AND_Gate
  or or_1 (ok, and_1_out, and_2_out);

  // Notes on the sheet:
  //   You must complete the circuit '16-bit ALU' instead.
  //   DO NOT EDIT THIS CIRCUIT!
endmodule

module _16_bit_ALU (
  input  [3:0] ALU_code,
  input  [15:0] a,
  input  [15:0] b,
  output [15:0] result,
  output overflow
);

  wire inverse_1_overflow, numeric_addition_1_overflow, numeric_subtraction_1_overflow,
       shift_left_arithmetic_1_overflow;
  wire [15:0] and_1_out, equals_1_out_3, greater_than_1_out_3, inverse_1_out, less_than_1_out_3, not_1_out,
       not_equals_1_out_3, numeric_addition_1_result, numeric_subtraction_1_result, or_1_out,
       shift_left_arithmetic_1_output, shift_left_logical_1_output, shift_right_arithmetic_1_output,
       shift_right_logical_1_output;

  assign or_1_out = a | b;  // OR_Gate or_1, 16 bits wide
  shift_right_arithmetic shift_right_arithmetic_1 (.Input(a), .Output(shift_right_arithmetic_1_output));
  shift_right_logical shift_right_logical_1 (.Input(a), .Output(shift_right_logical_1_output));
  shift_left_arithmetic shift_left_arithmetic_1 (
    .Input(a), .overflow(shift_left_arithmetic_1_overflow), .Output(shift_left_arithmetic_1_output));
  inverse inverse_1 (.In(a), .overflow(inverse_1_overflow), .out(inverse_1_out));
  shift_left_logical shift_left_logical_1 (.Input(a), .Output(shift_left_logical_1_output));
  equals equals_1 (.Input_1(a), .Input_2(b), .out_3(equals_1_out_3));
  not_equals not_equals_1 (.Input_1(a), .Input_2(b), .out_3(not_equals_1_out_3));
  less_than less_than_1 (.a(a), .b(b), .out_3(less_than_1_out_3));
  greater_than greater_than_1 (.a(a), .b(b), .out_3(greater_than_1_out_3));
  numeric_addition numeric_addition_1 (
    .a(a), .b(b), .overflow(numeric_addition_1_overflow), .result(numeric_addition_1_result));
  numeric_subtraction numeric_subtraction_1 (
    .a(a), .b(b), .overflow(numeric_subtraction_1_overflow), .result(numeric_subtraction_1_result));
  assign and_1_out = a & b;  // AND_Gate and_1, 16 bits wide
  assign not_1_out = ~a;  // NOT_Gate not_1, 16 bits wide
  Multiplexer #(.select(4), .width(16), .enable("false")) multiplexer_1 (
    .in0({16{1'b0}}), .in1(not_1_out), .in2(and_1_out), .in3(or_1_out), .in4(numeric_addition_1_result),
    .in5(numeric_subtraction_1_result), .in6(less_than_1_out_3), .in7(greater_than_1_out_3),
    .in8(equals_1_out_3), .in9(not_equals_1_out_3), .in10(inverse_1_out), .in11(shift_left_logical_1_output),
    .in12(shift_right_logical_1_output), .in13(shift_left_arithmetic_1_output),
    .in14(shift_right_arithmetic_1_output), .in15(a), .out(result), .sel(ALU_code));
  Multiplexer #(.select(4), .enable("false")) multiplexer_2 (
    .in0(1'b0), .in1(1'b0), .in2(1'b0), .in3(1'b0), .in4(numeric_addition_1_overflow),
    .in5(numeric_subtraction_1_overflow), .in6(1'b0), .in7(1'b0), .in8(1'b0), .in9(1'b0),
    .in10(inverse_1_overflow), .in11(1'b0), .in12(1'b0), .in13(shift_left_arithmetic_1_overflow),
    .in14(1'b0), .in15(1'b0), .out(overflow), .sel(ALU_code));

  // Notes on the sheet:
  //   This circuit is used as a block in the main circuit, and its layout must remain unchanged. The circuit called "main" should be the main circuit of this file.
  //   Do not change the circuit appearance.
  //   DO NOT CHANGE THE INPUTS AND OUTPUTS OF THIS CIRCUIT!
  //   Do not add/remove inputs or outputs. Do not even change their location or orientation.
endmodule

// +
module numeric_addition (
  input  [15:0] a,
  input  [15:0] b,
  output [15:0] result,
  output overflow
);

  wire and_1_out, and_2_out, not_1_out, not_2_out, not_3_out;

  not not_1 (not_1_out, a[15]);
  not not_2 (not_2_out, b[15]);
  _16_bit_carry u_16_bit_carry_1 (.a(a), .b(b), .s(result), .in_1(1'b0));  // open: P, G
  not not_3 (not_3_out, result[15]);
  and and_1 (and_1_out, a[15], b[15], not_3_out);
  or or_1 (overflow, and_1_out, and_2_out);
  and and_2 (and_2_out, not_1_out, not_2_out, result[15]);
endmodule

// -
module numeric_subtraction (
  input  [15:0] a,
  input  [15:0] b,
  output [15:0] result,
  output overflow
);

  wire and_1_out, and_2_out, not_2_out, not_3_out, not_4_out;
  wire [15:0] not_1_out;

  assign not_1_out = ~b;  // NOT_Gate not_1, 16 bits wide
  not not_2 (not_2_out, a[15]);
  not not_3 (not_3_out, not_1_out[15]);
  _16_bit_carry u_16_bit_carry_1 (.a(a), .b(not_1_out), .s(result), .in_1(1'b1));  // open: P, G
  not not_4 (not_4_out, result[15]);
  and and_1 (and_1_out, a[15], not_1_out[15], not_4_out);
  or or_1 (overflow, and_1_out, and_2_out);
  and and_2 (and_2_out, not_2_out, not_3_out, result[15]);
endmodule

module less_than (
  input  [15:0] a,
  input  [15:0] b,
  output [15:0] out_3
);

  wire and_1_out, and_2_out, and_3_out, bitselector_1_out, bitselector_2_out, bitselector_3_out, not_1_out,
       not_2_out, or_1_out;
  wire [15:0] numeric_subtraction_1_result;

  numeric_subtraction numeric_subtraction_1 (.a(a), .b(b), .result(numeric_subtraction_1_result));  // open: overflow
  BitSelector #(.width(16)) bitselector_1 (.in(a), .out(bitselector_1_out), .sel(4'b1111));
  not not_1 (not_1_out, bitselector_1_out);
  BitSelector #(.width(16)) bitselector_2 (.in(b), .out(bitselector_2_out), .sel(4'b1111));
  not not_2 (not_2_out, bitselector_2_out);
  BitSelector #(.width(16)) bitselector_3 (.in(numeric_subtraction_1_result), .out(bitselector_3_out), .sel(4'b1111));
  and and_1 (and_1_out, bitselector_2_out, bitselector_3_out, bitselector_1_out);
  and and_2 (and_2_out, not_2_out, bitselector_3_out, not_1_out);
  or or_1 (or_1_out, and_2_out, and_1_out, and_3_out);
  and and_3 (and_3_out, bitselector_1_out, not_2_out);
  Multiplexer #(.width(16), .enable("false")) multiplexer_1 (
    .in0({16{1'b0}}), .in1(16'h1), .out(out_3), .sel(or_1_out));
endmodule

module greater_than (
  input  [15:0] a,
  input  [15:0] b,
  output [15:0] out_3
);

  wire and_1_out, and_2_out, and_3_out, bitselector_1_out, bitselector_2_out, bitselector_3_out, not_1_out,
       not_2_out, or_1_out;
  wire [15:0] numeric_subtraction_1_result;

  numeric_subtraction numeric_subtraction_1 (.a(b), .b(a), .result(numeric_subtraction_1_result));  // open: overflow
  BitSelector #(.width(16)) bitselector_1 (.in(a), .out(bitselector_1_out), .sel(4'b1111));
  not not_1 (not_1_out, bitselector_1_out);
  BitSelector #(.width(16)) bitselector_2 (.in(b), .out(bitselector_2_out), .sel(4'b1111));
  not not_2 (not_2_out, bitselector_2_out);
  BitSelector #(.width(16)) bitselector_3 (.in(numeric_subtraction_1_result), .out(bitselector_3_out), .sel(4'b1111));
  and and_1 (and_1_out, not_2_out, bitselector_3_out, not_1_out);
  and and_2 (and_2_out, bitselector_2_out, bitselector_3_out, bitselector_1_out);
  or or_1 (or_1_out, and_1_out, and_2_out, and_3_out);
  and and_3 (and_3_out, not_1_out, bitselector_2_out);
  Multiplexer #(.width(16), .enable("false")) multiplexer_1 (
    .in0({16{1'b0}}), .in1(16'h1), .out(out_3), .sel(or_1_out));
endmodule

module equals (
  input  [15:0] Input_1,
  input  [15:0] Input_2,
  output [15:0] out_3
);

  wire and_1_out, xnor_1_out, xnor_2_out, xnor_3_out, xnor_4_out, xnor_5_out, xnor_6_out, xnor_7_out,
       xnor_8_out, xnor_9_out, xnor_10_out, xnor_11_out, xnor_12_out, xnor_13_out, xnor_14_out, xnor_15_out,
       xnor_16_out;

  xnor xnor_1 (xnor_1_out, Input_1[0], Input_2[0]);
  xnor xnor_2 (xnor_2_out, Input_1[1], Input_2[1]);
  xnor xnor_3 (xnor_3_out, Input_1[2], Input_2[2]);
  xnor xnor_4 (xnor_4_out, Input_1[3], Input_2[3]);
  xnor xnor_5 (xnor_5_out, Input_1[4], Input_2[4]);
  xnor xnor_6 (xnor_6_out, Input_1[5], Input_2[5]);
  xnor xnor_7 (xnor_7_out, Input_1[6], Input_2[6]);
  xnor xnor_8 (xnor_8_out, Input_1[7], Input_2[7]);
  xnor xnor_9 (xnor_9_out, Input_1[8], Input_2[8]);
  xnor xnor_10 (xnor_10_out, Input_1[9], Input_2[9]);
  xnor xnor_11 (xnor_11_out, Input_1[10], Input_2[10]);
  xnor xnor_12 (xnor_12_out, Input_1[11], Input_2[11]);
  xnor xnor_13 (xnor_13_out, Input_1[12], Input_2[12]);
  xnor xnor_14 (xnor_14_out, Input_1[13], Input_2[13]);
  xnor xnor_15 (xnor_15_out, Input_1[14], Input_2[14]);
  xnor xnor_16 (xnor_16_out, Input_1[15], Input_2[15]);
  and and_1 (and_1_out, xnor_1_out, xnor_2_out, xnor_3_out, xnor_4_out, xnor_5_out, xnor_6_out, xnor_7_out, xnor_8_out, xnor_9_out, xnor_10_out, xnor_11_out, xnor_12_out, xnor_13_out, xnor_14_out, xnor_15_out, xnor_16_out);
  Multiplexer #(.width(16), .enable("false")) multiplexer_1 (
    .in0({16{1'b0}}), .in1(16'h1), .out(out_3), .sel(and_1_out));

  // Other names for the same wires on the sheet: _1_9 = Input_1[9]; _1_10 = Input_1[10]; _1_11 = Input_1[11];
  //   _1_12 = Input_1[12]; _1_13 = Input_1[13]; _1_14 = Input_1[14]; _1_15 = Input_1[15]; _2_0 = Input_2[0];
  //   _2_1 = Input_2[1]; _2_2 = Input_2[2]; _2_3 = Input_2[3]; _2_4 = Input_2[4]; _2_5 = Input_2[5];
  //   _2_6 = Input_2[6]
endmodule

module inverse (
  input  [15:0] In,
  output [15:0] out,
  output overflow
);

  wire [15:0] not_1_out;

  numeric_addition numeric_addition_1 (.a(16'h1), .b(not_1_out), .overflow(overflow), .result(out));
  assign not_1_out = ~In;  // NOT_Gate not_1, 16 bits wide
endmodule

module shift_left_logical (
  input  [15:0] Input,
  output [15:0] Output
);


  assign Output = {Input[14:0], 1'b0};
endmodule

module shift_right_logical (
  input  [15:0] Input,
  output [15:0] Output
);


  assign Output = {1'b0, Input[15:1]};
endmodule

module shift_left_arithmetic (
  input  [15:0] Input,
  output [15:0] Output,
  output overflow
);

  xor xor_1 (overflow, Input[14], Input[15]);

  assign Output = {Input[14:0], 1'b0};
endmodule

module shift_right_arithmetic (
  input  [15:0] Input,
  output [15:0] Output
);


  assign Output = {{2{Input[15]}}, Input[14:1]};
endmodule

module not_equals (
  input  [15:0] Input_1,
  input  [15:0] Input_2,
  output [15:0] out_3
);

  wire and_1_out, not_1_out, xnor_1_out, xnor_2_out, xnor_3_out, xnor_4_out, xnor_5_out, xnor_6_out,
       xnor_7_out, xnor_8_out, xnor_9_out, xnor_10_out, xnor_11_out, xnor_12_out, xnor_13_out, xnor_14_out,
       xnor_15_out, xnor_16_out;

  xnor xnor_1 (xnor_1_out, Input_1[0], Input_2[0]);
  xnor xnor_2 (xnor_2_out, Input_1[1], Input_2[1]);
  xnor xnor_3 (xnor_3_out, Input_1[2], Input_2[2]);
  xnor xnor_4 (xnor_4_out, Input_1[3], Input_2[3]);
  xnor xnor_5 (xnor_5_out, Input_1[4], Input_2[4]);
  xnor xnor_6 (xnor_6_out, Input_1[5], Input_2[5]);
  xnor xnor_7 (xnor_7_out, Input_1[6], Input_2[6]);
  xnor xnor_8 (xnor_8_out, Input_1[7], Input_2[7]);
  xnor xnor_9 (xnor_9_out, Input_1[8], Input_2[8]);
  xnor xnor_10 (xnor_10_out, Input_1[9], Input_2[9]);
  xnor xnor_11 (xnor_11_out, Input_1[10], Input_2[10]);
  xnor xnor_12 (xnor_12_out, Input_1[11], Input_2[11]);
  xnor xnor_13 (xnor_13_out, Input_1[12], Input_2[12]);
  xnor xnor_14 (xnor_14_out, Input_1[13], Input_2[13]);
  xnor xnor_15 (xnor_15_out, Input_1[14], Input_2[14]);
  xnor xnor_16 (xnor_16_out, Input_1[15], Input_2[15]);
  and and_1 (and_1_out, xnor_1_out, xnor_2_out, xnor_3_out, xnor_4_out, xnor_5_out, xnor_6_out, xnor_7_out, xnor_8_out, xnor_9_out, xnor_10_out, xnor_11_out, xnor_12_out, xnor_13_out, xnor_14_out, xnor_15_out, xnor_16_out);
  Multiplexer #(.width(16), .enable("false")) multiplexer_1 (
    .in0({16{1'b0}}), .in1(16'h1), .out(out_3), .sel(not_1_out));
  not not_1 (not_1_out, and_1_out);

  // Other names for the same wires on the sheet: _1_9 = Input_1[9]; _1_10 = Input_1[10]; _1_11 = Input_1[11];
  //   _1_12 = Input_1[12]; _1_13 = Input_1[13]; _1_14 = Input_1[14]; _1_15 = Input_1[15]; _2_0 = Input_2[0];
  //   _2_1 = Input_2[1]; _2_2 = Input_2[2]; _2_3 = Input_2[3]; _2_4 = Input_2[4]; _2_5 = Input_2[5];
  //   _2_6 = Input_2[6]
endmodule
