// Logisim project Adders.circ as structural Verilog: 7 circuits, main circuit main
module main (
  input  c,
  input  [15:0] a,
  input  [15:0] b,
  output [15:0] Carry_Output,
  output [15:0] Riple_Output
);

  _16_bit_ripple u_16_bit_ripple_1 (.a(b), .b(a), .CarryIn(c), .S(Riple_Output));  // open: Overflow
  _16_bit_carry u_16_bit_carry_1 (.a(a), .b(b), .s(Carry_Output), .in_1(c));  // open: P, G
endmodule

module _1_bit_adder (
  input  CarryIn,
  input  A,
  input  B,
  output Sum,
  output CarryOut
);

  wire and_1_out, and_2_out, and_3_out, and_4_out, and_5_out, and_6_out, and_7_out, not_1_out, not_2_out,
       not_3_out;

  not not_1 (not_1_out, A);
  not not_2 (not_2_out, B);
  not not_3 (not_3_out, CarryIn);
  and and_1 (and_1_out, A, not_2_out, not_3_out);
  and and_2 (and_2_out, not_1_out, B, not_3_out);
  and and_3 (and_3_out, A, B, CarryIn);
  and and_4 (and_4_out, not_1_out, not_2_out, CarryIn);
  and and_5 (and_5_out, A, CarryIn);
  and and_6 (and_6_out, B, CarryIn);
  or or_1 (CarryOut, and_5_out, and_6_out, and_7_out);
  or or_2 (Sum, and_3_out, and_4_out, and_2_out, and_1_out);
  and and_7 (and_7_out, A, B);
endmodule

module _16_bit_ripple (
  input  CarryIn,
  input  [15:0] a,
  input  [15:0] b,
  output [15:0] S,
  output Overflow
);

  wire n1_bit_adder_1_carryout, n1_bit_adder_2_carryout, n1_bit_adder_3_carryout, n1_bit_adder_4_carryout,
       n1_bit_adder_5_carryout, n1_bit_adder_6_carryout, n1_bit_adder_7_carryout, n1_bit_adder_8_carryout,
       n1_bit_adder_9_carryout, n1_bit_adder_10_carryout, n1_bit_adder_11_carryout, n1_bit_adder_12_carryout,
       n1_bit_adder_13_carryout, n1_bit_adder_14_carryout, n1_bit_adder_15_carryout;

  _1_bit_adder u_1_bit_adder_1 (.A(a[0]), .B(b[0]), .CarryIn(CarryIn), .CarryOut(n1_bit_adder_1_carryout), .Sum(S[0]));
  _1_bit_adder u_1_bit_adder_2 (
    .A(a[1]), .B(b[1]), .CarryIn(n1_bit_adder_1_carryout), .CarryOut(n1_bit_adder_2_carryout), .Sum(S[1]));
  _1_bit_adder u_1_bit_adder_3 (
    .A(a[2]), .B(b[2]), .CarryIn(n1_bit_adder_2_carryout), .CarryOut(n1_bit_adder_3_carryout), .Sum(S[2]));
  _1_bit_adder u_1_bit_adder_4 (
    .A(a[3]), .B(b[3]), .CarryIn(n1_bit_adder_3_carryout), .CarryOut(n1_bit_adder_4_carryout), .Sum(S[3]));
  _1_bit_adder u_1_bit_adder_5 (
    .A(a[4]), .B(b[4]), .CarryIn(n1_bit_adder_4_carryout), .CarryOut(n1_bit_adder_5_carryout), .Sum(S[4]));
  _1_bit_adder u_1_bit_adder_6 (
    .A(a[5]), .B(b[5]), .CarryIn(n1_bit_adder_5_carryout), .CarryOut(n1_bit_adder_6_carryout), .Sum(S[5]));
  _1_bit_adder u_1_bit_adder_7 (
    .A(a[6]), .B(b[6]), .CarryIn(n1_bit_adder_6_carryout), .CarryOut(n1_bit_adder_7_carryout), .Sum(S[6]));
  _1_bit_adder u_1_bit_adder_8 (
    .A(a[7]), .B(b[7]), .CarryIn(n1_bit_adder_7_carryout), .CarryOut(n1_bit_adder_8_carryout), .Sum(S[7]));
  _1_bit_adder u_1_bit_adder_9 (
    .A(a[8]), .B(b[8]), .CarryIn(n1_bit_adder_8_carryout), .CarryOut(n1_bit_adder_9_carryout), .Sum(S[8]));
  _1_bit_adder u_1_bit_adder_10 (
    .A(a[9]), .B(b[9]), .CarryIn(n1_bit_adder_9_carryout), .CarryOut(n1_bit_adder_10_carryout), .Sum(S[9]));
  _1_bit_adder u_1_bit_adder_11 (
    .A(a[10]), .B(b[10]), .CarryIn(n1_bit_adder_10_carryout), .CarryOut(n1_bit_adder_11_carryout), .Sum(S[10]));
  _1_bit_adder u_1_bit_adder_12 (
    .A(a[11]), .B(b[11]), .CarryIn(n1_bit_adder_11_carryout), .CarryOut(n1_bit_adder_12_carryout), .Sum(S[11]));
  _1_bit_adder u_1_bit_adder_13 (
    .A(a[12]), .B(b[12]), .CarryIn(n1_bit_adder_12_carryout), .CarryOut(n1_bit_adder_13_carryout), .Sum(S[12]));
  _1_bit_adder u_1_bit_adder_14 (
    .A(a[13]), .B(b[13]), .CarryIn(n1_bit_adder_13_carryout), .CarryOut(n1_bit_adder_14_carryout), .Sum(S[13]));
  _1_bit_adder u_1_bit_adder_15 (
    .A(a[14]), .B(b[14]), .CarryIn(n1_bit_adder_14_carryout), .CarryOut(n1_bit_adder_15_carryout), .Sum(S[14]));
  _1_bit_adder u_1_bit_adder_16 (
    .A(a[15]), .B(b[15]), .CarryIn(n1_bit_adder_15_carryout), .CarryOut(Overflow), .Sum(S[15]));
endmodule

module _4_bit_adder (
  input  CarryIn,
  input  [3:0] a,
  input  [3:0] b,
  output [3:0] S,
  output P0,
  output G0
);

  wire and_1_out, and_2_out, and_3_out, and_4_out, and_5_out, and_6_out, and_7_out, and_8_out, and_9_out,
       and_10_out, and_11_out, and_12_out, and_14_out, and_15_out, and_16_out, and_17_out, and_18_out,
       and_19_out, and_20_out, and_21_out, and_22_out, and_23_out, and_24_out, and_25_out, and_26_out,
       and_27_out, not_1_out, not_2_out, not_3_out, not_4_out, not_5_out, not_6_out, not_7_out, not_8_out,
       not_9_out, not_10_out, not_11_out, not_12_out, or_1_out, or_2_out, or_3_out, or_4_out, or_7_out,
       or_8_out, or_9_out;

  or or_1 (or_1_out, and_1_out, and_2_out);
  not not_1 (not_1_out, a[0]);
  not not_2 (not_2_out, b[0]);
  not not_3 (not_3_out, CarryIn);
  and and_1 (and_1_out, a[0], b[0]);
  and and_2 (and_2_out, or_3_out, CarryIn);
  not not_4 (not_4_out, a[1]);
  not not_5 (not_5_out, b[1]);
  not not_6 (not_6_out, or_1_out);
  and and_3 (and_3_out, a[1], b[1]);
  and and_4 (and_4_out, or_1_out, or_4_out);
  or or_2 (or_2_out, and_3_out, and_4_out);
  or or_3 (or_3_out, a[0], b[0]);
  or or_4 (or_4_out, a[1], b[1]);
  and and_5 (and_5_out, a[0], not_2_out, not_3_out);
  and and_6 (and_6_out, not_1_out, b[0], not_3_out);
  and and_7 (and_7_out, not_4_out, b[1], not_6_out);
  and and_8 (and_8_out, a[1], not_5_out, not_6_out);
  and and_9 (and_9_out, a[0], b[0], CarryIn);
  and and_10 (and_10_out, not_1_out, not_2_out, CarryIn);
  and and_11 (and_11_out, not_4_out, not_5_out, or_1_out);
  and and_12 (and_12_out, a[1], b[1], or_1_out);
  or or_5 (S[0], and_9_out, and_10_out, and_6_out, and_5_out);
  or or_6 (S[1], and_12_out, and_11_out, and_7_out, and_8_out);
  or or_7 (or_7_out, and_14_out, and_15_out);
  and and_13 (P0, or_3_out, or_4_out, or_8_out, or_9_out);
  not not_7 (not_7_out, a[2]);
  not not_8 (not_8_out, b[2]);
  not not_9 (not_9_out, or_2_out);
  and and_14 (and_14_out, a[2], b[2]);
  and and_15 (and_15_out, or_8_out, or_2_out);
  not not_10 (not_10_out, b[3]);
  not not_11 (not_11_out, a[3]);
  not not_12 (not_12_out, or_7_out);
  and and_16 (and_16_out, b[3], a[3]);
  and and_17 (and_17_out, or_9_out, and_14_out);
  or or_8 (or_8_out, a[2], b[2]);
  or or_9 (or_9_out, b[3], a[3]);
  and and_18 (and_18_out, or_9_out, or_8_out, and_3_out);
  or or_10 (G0, and_16_out, and_17_out, and_18_out, and_23_out);
  and and_19 (and_19_out, not_7_out, b[2], not_9_out);
  and and_20 (and_20_out, a[2], not_8_out, not_9_out);
  and and_21 (and_21_out, b[3], not_11_out, not_12_out);
  and and_22 (and_22_out, not_10_out, a[3], not_12_out);
  and and_23 (and_23_out, or_9_out, or_8_out, or_4_out, and_1_out);
  and and_24 (and_24_out, a[2], b[2], or_2_out);
  and and_25 (and_25_out, not_7_out, not_8_out, or_2_out);
  and and_26 (and_26_out, b[3], a[3], or_7_out);
  and and_27 (and_27_out, not_10_out, not_11_out, or_7_out);
  or or_11 (S[2], and_24_out, and_25_out, and_19_out, and_20_out);
  or or_12 (S[3], and_26_out, and_27_out, and_22_out, and_21_out);
endmodule

module _4_bit_adder_Optimised (
  input  c0,
  input  [3:0] a,
  input  [3:0] b,
  output [3:0] out_4
);

  wire and_1_out, and_2_out, and_3_out, and_4_out, and_5_out, and_6_out, and_7_out, and_8_out, and_9_out,
       and_10_out, and_11_out, and_12_out, and_13_out, and_14_out, and_15_out, and_16_out, and_17_out,
       and_18_out, and_19_out, and_20_out, and_21_out, and_22_out, and_23_out, and_24_out, and_25_out,
       and_26_out, and_27_out, and_28_out, and_29_out, and_30_out, and_31_out, and_32_out, and_33_out,
       and_34_out, and_35_out, and_36_out, and_37_out, and_38_out, and_39_out, and_40_out, and_41_out,
       and_42_out, and_43_out, and_44_out, and_45_out, and_46_out, not_1_out, not_2_out, not_3_out,
       not_4_out, not_5_out, not_6_out, not_7_out, not_8_out, not_9_out, not_10_out, not_11_out, or_2_out,
       or_4_out;

  not not_1 (not_1_out, a[3]);
  not not_2 (not_2_out, b[3]);
  and and_1 (and_1_out, a[3], not_2_out, not_8_out);
  and and_2 (and_2_out, not_1_out, b[3], not_8_out);
  not not_3 (not_3_out, a[0]);
  not not_4 (not_4_out, b[0]);
  not not_5 (not_5_out, c0);
  not not_6 (not_6_out, a[1]);
  not not_7 (not_7_out, b[1]);
  and and_3 (and_3_out, not_1_out, not_2_out, or_4_out);
  and and_4 (and_4_out, or_4_out, a[3], b[3]);
  not not_8 (not_8_out, or_4_out);
  or or_1 (out_4[3], and_4_out, and_3_out, and_2_out, and_1_out);
  and and_5 (and_5_out, a[1], b[1]);
  and and_6 (and_6_out, a[0], b[0], a[1]);
  and and_7 (and_7_out, a[0], b[0], b[1]);
  and and_8 (and_8_out, a[0], c0, a[1]);
  and and_9 (and_9_out, a[0], c0, b[1]);
  and and_10 (and_10_out, b[0], c0, a[1]);
  and and_11 (and_11_out, b[0], c0, b[1]);
  or or_2 (or_2_out, and_5_out, and_6_out, and_7_out, and_8_out, and_9_out, and_10_out, and_11_out);
  not not_9 (not_9_out, or_2_out);
  not not_10 (not_10_out, a[2]);
  not not_11 (not_11_out, b[2]);
  and and_12 (and_12_out, a[2], not_11_out, not_9_out);
  and and_13 (and_13_out, not_10_out, b[2], not_9_out);
  and and_14 (and_14_out, not_10_out, not_11_out, or_2_out);
  and and_15 (and_15_out, or_2_out, a[2], b[2]);
  and and_16 (and_16_out, not_3_out, not_4_out, a[1], not_7_out);
  and and_17 (and_17_out, a[2], b[2]);
  or or_3 (out_4[2], and_15_out, and_14_out, and_13_out, and_12_out);
  and and_18 (and_18_out, a[0], b[0], not_6_out, not_7_out);
  and and_19 (and_19_out, not_3_out, not_4_out, a[1], b[1]);
  and and_20 (and_20_out, a[2], a[1], b[1]);
  and and_21 (and_21_out, a[2], a[1], a[0], b[0]);
  and and_22 (and_22_out, b[2], a[1], b[1]);
  and and_23 (and_23_out, a[0], b[0], a[1], b[1]);
  and and_24 (and_24_out, a[2], b[1], a[0], b[0]);
  and and_25 (and_25_out, not_3_out, not_5_out, not_6_out, b[1]);
  and and_26 (and_26_out, not_3_out, not_5_out, a[1], not_7_out);
  and and_27 (and_27_out, b[2], b[1], a[0], b[0]);
  and and_28 (and_28_out, a[1], b[2], a[0], b[0]);
  and and_29 (and_29_out, a[0], c0, not_6_out, not_7_out);
  and and_30 (and_30_out, a[2], a[1], a[0], c0);
  or or_4 (or_4_out, and_17_out, and_20_out, and_22_out, and_21_out, and_24_out, and_28_out, and_27_out, and_30_out, and_33_out, and_34_out, and_38_out, and_37_out, and_40_out, and_44_out, and_43_out);
  and and_31 (and_31_out, a[0], c0, a[1], b[1]);
  and and_32 (and_32_out, not_4_out, not_5_out, a[1], not_7_out);
  and and_33 (and_33_out, a[2], b[1], a[0], c0);
  and and_34 (and_34_out, a[1], b[2], a[0], c0);
  and and_35 (and_35_out, not_4_out, not_5_out, not_6_out, b[1]);
  and and_36 (and_36_out, b[0], c0, not_6_out, not_7_out);
  and and_37 (and_37_out, a[2], a[1], b[0], c0);
  and and_38 (and_38_out, b[2], b[1], a[0], c0);
  and and_39 (and_39_out, b[0], c0, a[1], b[1]);
  and and_40 (and_40_out, a[2], b[1], b[0], c0);
  and and_41 (and_41_out, not_3_out, b[0], not_5_out);
  and and_42 (and_42_out, a[0], not_4_out, not_5_out);
  or or_5 (out_4[0], and_42_out, and_41_out, and_46_out, and_45_out);
  and and_43 (and_43_out, b[1], b[2], b[0], c0);
  and and_44 (and_44_out, a[1], b[2], b[0], c0);
  and and_45 (and_45_out, a[0], b[0], c0);
  and and_46 (and_46_out, not_3_out, not_4_out, c0);
  or or_6 (out_4[1], and_39_out, and_36_out, and_35_out, and_32_out, and_31_out, and_29_out, and_25_out, and_26_out, and_23_out, and_18_out, and_19_out, and_16_out);
endmodule

module _16_bit_carry (
  input  in_1,
  input  [15:0] a,
  input  [15:0] b,
  output [15:0] s,
  output P,
  output G
);

  wire and_1_out, and_2_out, and_3_out, and_4_out, and_5_out, and_6_out, n4_bit_adder_1_g0,
       n4_bit_adder_1_p0, n4_bit_adder_2_g0, n4_bit_adder_2_p0, n4_bit_adder_3_g0, n4_bit_adder_3_p0,
       or_1_out, or_2_out, or_3_out;

  and and_1 (and_1_out, and_5_out, n4_bit_adder_3_p0);
  and and_2 (and_2_out, and_4_out, n4_bit_adder_3_p0);
  _4_bit_adder u_4_bit_adder_1 (
    .a(a[3:0]), .b(b[3:0]), .CarryIn(in_1), .P0(n4_bit_adder_1_p0), .G0(n4_bit_adder_1_g0), .S(s[3:0]));
  and and_3 (and_3_out, in_1, n4_bit_adder_1_p0);
  or or_1 (or_1_out, and_3_out, n4_bit_adder_1_g0);
  _4_bit_adder u_4_bit_adder_2 (
    .a(a[7:4]), .b(b[7:4]), .CarryIn(or_1_out), .P0(n4_bit_adder_2_p0), .G0(n4_bit_adder_2_g0), .S(s[7:4]));
  and and_4 (and_4_out, n4_bit_adder_1_g0, n4_bit_adder_2_p0);
  and and_5 (and_5_out, and_3_out, n4_bit_adder_2_p0);
  or or_2 (or_2_out, and_5_out, and_4_out, n4_bit_adder_2_g0);
  _4_bit_adder u_4_bit_adder_3 (
    .a(a[11:8]), .b(b[11:8]), .CarryIn(or_2_out), .P0(n4_bit_adder_3_p0), .G0(n4_bit_adder_3_g0), .S(s[11:8]));
  and and_6 (and_6_out, n4_bit_adder_2_g0, n4_bit_adder_3_p0);
  or or_3 (or_3_out, and_1_out, and_2_out, and_6_out, n4_bit_adder_3_g0);
  _4_bit_adder u_4_bit_adder_4 (.a(a[15:12]), .b(b[15:12]), .CarryIn(or_3_out), .P0(P), .G0(G), .S(s[15:12]));
endmodule

module _16_bit_ripple_BUS (
  input  CarryIn,
  input  [15:0] a,
  input  [15:0] b,
  output Out__C0,
  output Out__C8,
  output Out__C1,
  output Out__C9,
  output Out__C2,
  output Out__C10,
  output Out__C3,
  output Out__C11,
  output Out__C4,
  output Out__C12,
  output Out__C5,
  output Out__C13,
  output Out__C6,
  output Out__C14,
  output Out__C7,
  output Out__C15,
  output CarryOut
);

  wire n1_bit_adder_1_carryout, n1_bit_adder_2_carryout, n1_bit_adder_3_carryout, n1_bit_adder_4_carryout,
       n1_bit_adder_5_carryout, n1_bit_adder_6_carryout, n1_bit_adder_7_carryout, n1_bit_adder_8_carryout,
       n1_bit_adder_9_carryout, n1_bit_adder_10_carryout, n1_bit_adder_11_carryout, n1_bit_adder_12_carryout,
       n1_bit_adder_13_carryout, n1_bit_adder_14_carryout, n1_bit_adder_15_carryout, or_1_out;

  or or_1 (or_1_out, CarryIn, CarryOut);
  _1_bit_adder u_1_bit_adder_1 (
    .A(a[0]), .B(b[0]), .CarryIn(or_1_out), .CarryOut(n1_bit_adder_1_carryout), .Sum(Out__C0));
  _1_bit_adder u_1_bit_adder_2 (
    .A(a[1]), .B(b[1]), .CarryIn(n1_bit_adder_1_carryout), .CarryOut(n1_bit_adder_2_carryout), .Sum(Out__C1));
  _1_bit_adder u_1_bit_adder_3 (
    .A(a[2]), .B(b[2]), .CarryIn(n1_bit_adder_2_carryout), .CarryOut(n1_bit_adder_3_carryout), .Sum(Out__C2));
  _1_bit_adder u_1_bit_adder_4 (
    .A(a[3]), .B(b[3]), .CarryIn(n1_bit_adder_3_carryout), .CarryOut(n1_bit_adder_4_carryout), .Sum(Out__C3));
  _1_bit_adder u_1_bit_adder_5 (
    .A(a[4]), .B(b[4]), .CarryIn(n1_bit_adder_4_carryout), .CarryOut(n1_bit_adder_5_carryout), .Sum(Out__C4));
  _1_bit_adder u_1_bit_adder_6 (
    .A(a[5]), .B(b[5]), .CarryIn(n1_bit_adder_5_carryout), .CarryOut(n1_bit_adder_6_carryout), .Sum(Out__C5));
  _1_bit_adder u_1_bit_adder_7 (
    .A(a[6]), .B(b[6]), .CarryIn(n1_bit_adder_6_carryout), .CarryOut(n1_bit_adder_7_carryout), .Sum(Out__C6));
  _1_bit_adder u_1_bit_adder_8 (
    .A(a[7]), .B(b[7]), .CarryIn(n1_bit_adder_7_carryout), .CarryOut(n1_bit_adder_8_carryout), .Sum(Out__C7));
  _1_bit_adder u_1_bit_adder_9 (
    .A(a[8]), .B(b[8]), .CarryIn(n1_bit_adder_8_carryout), .CarryOut(n1_bit_adder_9_carryout), .Sum(Out__C8));
  _1_bit_adder u_1_bit_adder_10 (
    .A(a[9]), .B(b[9]), .CarryIn(n1_bit_adder_9_carryout), .CarryOut(n1_bit_adder_10_carryout), .Sum(Out__C9));
  _1_bit_adder u_1_bit_adder_11 (
    .A(a[10]), .B(b[10]), .CarryIn(n1_bit_adder_10_carryout), .CarryOut(n1_bit_adder_11_carryout),
    .Sum(Out__C10));
  _1_bit_adder u_1_bit_adder_12 (
    .A(a[11]), .B(b[11]), .CarryIn(n1_bit_adder_11_carryout), .CarryOut(n1_bit_adder_12_carryout),
    .Sum(Out__C11));
  _1_bit_adder u_1_bit_adder_13 (
    .A(a[12]), .B(b[12]), .CarryIn(n1_bit_adder_12_carryout), .CarryOut(n1_bit_adder_13_carryout),
    .Sum(Out__C12));
  _1_bit_adder u_1_bit_adder_14 (
    .A(a[13]), .B(b[13]), .CarryIn(n1_bit_adder_13_carryout), .CarryOut(n1_bit_adder_14_carryout),
    .Sum(Out__C13));
  _1_bit_adder u_1_bit_adder_15 (
    .A(a[14]), .B(b[14]), .CarryIn(n1_bit_adder_14_carryout), .CarryOut(n1_bit_adder_15_carryout),
    .Sum(Out__C14));
  _1_bit_adder u_1_bit_adder_16 (
    .A(a[15]), .B(b[15]), .CarryIn(n1_bit_adder_15_carryout), .CarryOut(CarryOut), .Sum(Out__C15));
endmodule
