// Logisim project FullDatapath.circ as structural Verilog: 8 circuits, main circuit main
module main (
  output [15:0] pc,
  output [15:0] r0,
  output [15:0] r1,
  output [15:0] r2,
  output [15:0] r3,
  output [15:0] r4,
  output [15:0] r5,
  output [15:0] r6,
  output [15:0] r7,
  output [15:0] r8,
  output [15:0] r9,
  output [15:0] r10,
  output [15:0] r11,
  output [15:0] r12,
  output [15:0] r13,
  output [15:0] r14,
  output [15:0] r15,
  output halt
);

  wire and_1_out, and_2_out, bitselector_1_out, clock_1_out, control_unit_16_bit_1_alu_input_selector,
       control_unit_16_bit_1_brnz, control_unit_16_bit_1_exception_trower, control_unit_16_bit_1_jal,
       control_unit_16_bit_1_jr, control_unit_16_bit_1_jump, control_unit_16_bit_1_lw,
       control_unit_16_bit_1_sw, control_unit_16_bit_1_write_disable, imm, not_1_out, oflow, or_1_out,
       or_2_out, reset_out;
  wire [3:0] control_unit_16_bit_1_alu_op_code, control_unit_16_bit_1_rd, control_unit_16_bit_1_rs,
       control_unit_16_bit_1_rt;
  wire [15:0] control_unit_16_bit_1_bit_extend, multiplexer_1_out, multiplexer_2_out, multiplexer_3_out,
       multiplexer_4_out, multiplexer_5_out, multiplexer_7_out, n16_bit_alu_1_p2, n16_bit_alu_1_p4,
       n16_bit_carry_1_s, n16_bit_file_register_modified_1_rs_output,
       n16_bit_file_register_modified_1_rt_output, ram_1_data, ram_2_data;

  Halt halt_1 (.instruction(ram_1_data), .ALU_overflow(or_1_out), .clock(clock_1_out), .reset(reset_out), .halt(halt));
  Clock clock_1 (.out(clock_1_out));
  or or_1 (or_1_out, control_unit_16_bit_1_exception_trower, oflow);
  Button reset (.out(reset_out));
  and and_1 (and_1_out, ~halt, clock_1_out);  // AND_Gate
  Multiplexer #(.width(16), .enable("false")) multiplexer_1 (
    .in0(control_unit_16_bit_1_bit_extend), .in1(multiplexer_2_out), .out(multiplexer_1_out),
    .sel(control_unit_16_bit_1_jump));
  _16_bit_program_counter__PC u_16_bit_program_counter_pc_1 (
    .Clock(and_1_out), .Branch_absolute(control_unit_16_bit_1_jump), .Branch_relative(and_2_out),
    .Reset(reset_out), .Branch_value(multiplexer_1_out), .Instruction_address(pc));
  RAM #(.addrWidth(16), .dataWidth(16)) ram_1 (
    .addr(pc), .data(ram_1_data), .clk(and_1_out), .ld(1'b1));  // open: sel, clr
  Multiplexer #(.width(16), .enable("false")) multiplexer_2 (
    .in0(control_unit_16_bit_1_bit_extend), .in1(n16_bit_alu_1_p4), .out(multiplexer_2_out),
    .sel(control_unit_16_bit_1_jr));
  and and_2 (and_2_out, control_unit_16_bit_1_brnz, bitselector_1_out);
  Control_unit___16_bit control_unit_16_bit_1 (
    .in_1(ram_1_data), .Bit_extend(control_unit_16_bit_1_bit_extend), .rs(control_unit_16_bit_1_rs),
    .rt(control_unit_16_bit_1_rt), .lw(control_unit_16_bit_1_lw), .sw(control_unit_16_bit_1_sw),
    .ALU_input_selector(control_unit_16_bit_1_alu_input_selector),
    .ALU_op_code(control_unit_16_bit_1_alu_op_code), .rd(control_unit_16_bit_1_rd),
    .brnz(control_unit_16_bit_1_brnz), .jump(control_unit_16_bit_1_jump), .jr(control_unit_16_bit_1_jr),
    .imm(imm), .jal(control_unit_16_bit_1_jal), .Write_Disable(control_unit_16_bit_1_write_disable),
    .Exception_trower(control_unit_16_bit_1_exception_trower));
  BitSelector #(.width(16)) bitselector_1 (.in(n16_bit_alu_1_p4), .out(bitselector_1_out), .sel(4'b0000));
  _16_bit_carry u_16_bit_carry_1 (.a(pc), .b({16{1'b0}}), .s(n16_bit_carry_1_s), .in_1(1'b1));  // open: P, G
  Multiplexer #(.width(16), .enable("false")) multiplexer_3 (
    .in0(multiplexer_5_out), .in1(n16_bit_carry_1_s), .out(multiplexer_3_out), .sel(control_unit_16_bit_1_jal));
  not not_1 (not_1_out, or_2_out);
  or or_2 (or_2_out, control_unit_16_bit_1_write_disable, oflow, control_unit_16_bit_1_sw);
  _16_bit_file_register_modified u_16_bit_file_register_modified_1 (
    .rs_output(n16_bit_file_register_modified_1_rs_output), .rd(control_unit_16_bit_1_rd), .write(not_1_out),
    .rt_output(n16_bit_file_register_modified_1_rt_output), .Clock(and_1_out), .reset(reset_out),
    .rs(control_unit_16_bit_1_rs), .rt(control_unit_16_bit_1_rt), .r0(r0), .r1(r1), .r2(r2), .r3(r3),
    .r4(r4), .r5(r5), .r6(r6), .r7(r7), .r8(r8), .r9(r9), .r10(r10), .r11(r11), .r12(r12), .r13(r13),
    .r14(r14), .r15(r15), .data(multiplexer_3_out));
  Multiplexer #(.width(16), .enable("false")) multiplexer_4 (
    .in0(n16_bit_file_register_modified_1_rt_output), .in1(control_unit_16_bit_1_bit_extend),
    .out(multiplexer_4_out), .sel(control_unit_16_bit_1_alu_input_selector));
  Multiplexer #(.width(16), .enable("false")) multiplexer_5 (
    .in0(multiplexer_7_out), .in1(ram_2_data), .out(multiplexer_5_out), .sel(control_unit_16_bit_1_lw));
  // _16_bit_ALU 16_bit_alu_1: pin names not known; wires that end beside it: n16_bit_file_register_modified_1_rs_output, n16_bit_alu_1_p2, control_unit_16_bit_1_alu_op_code, n16_bit_alu_1_p4, oflow
  Multiplexer #(.width(16), .enable("false")) multiplexer_6 (
    .in0(multiplexer_4_out), .in1({16{1'b0}}), .out(n16_bit_alu_1_p2), .sel(control_unit_16_bit_1_brnz));
  Multiplexer #(.width(16), .enable("false")) multiplexer_7 (
    .in0(n16_bit_alu_1_p4), .in1(control_unit_16_bit_1_bit_extend), .out(multiplexer_7_out), .sel(imm));
  RAM #(.addrWidth(16), .dataWidth(16), .bus("separate")) ram_2 (
    .addr(n16_bit_alu_1_p4), .din(n16_bit_file_register_modified_1_rt_output), .data(ram_2_data),
    .str(control_unit_16_bit_1_sw), .clk(and_1_out), .ld(control_unit_16_bit_1_lw), .clr(reset_out));  // open: sel

  // Notes on the sheet:
  //   current instruction
  //   clock signal
  //   reset button
  //   DO NOT CHANGE THE INPUTS AND OUTPUTS OF THIS CIRCUIT! Do not add/remove inputs or outputs. Do not even change their location or orientation.
endmodule

module Halt (
  input  [15:0] instruction,
  input  clock,
  input  reset,
  input  ALU_overflow,
  output halt
);

  wire and_1_out, comparator_1_eq, comparator_2_gt, counter_1_carry, or_1_out, or_2_out;
  wire [11:0] counter_1_q;

  Comparator #(.width(16), .mode("unsigned")) comparator_1 (
    .a(instruction), .b({16{1'b0}}), .eq(comparator_1_eq));  // open: gt, lt
  Counter #(.width(12), .max('hfff), .trigger("falling")) counter_1 (
    .Q(counter_1_q), .carry(counter_1_carry), .clk(clock), .clr(reset));  // open: load, D, count
  or or_1 (or_1_out, comparator_1_eq, counter_1_carry);
  Comparator #(.width(12), .mode("unsigned")) comparator_2 (
    .a(counter_1_q), .b({12{1'b0}}), .gt(comparator_2_gt));  // open: eq, lt
  or or_2 (or_2_out, halt, ALU_overflow, and_1_out);
  and and_1 (and_1_out, or_1_out, comparator_2_gt);
  Register #(.width(1)) register_1 (.D(or_2_out), .Q(halt), .clk(clock), .clr(reset));  // open: en

  // Notes on the sheet:
  //   halt becomes and stays asserted if the instruction is 0000 (not in the first clock cycle) or the end of the counter is reached (2^12)
endmodule

module _16_bit_program_counter__PC (
  input  Clock,
  input  Branch_absolute,
  input  Branch_relative,
  input  Reset,
  input  [15:0] Branch_value,
  output [15:0] Instruction_address
);

  wire not_1_out, not_2_out;
  wire [1:0] and_2_out;
  wire [15:0] multiplexer_1_out, n16_bit_carry_1_s, n16_bit_carry_2_s;

  not not_1 (not_1_out, Branch_absolute);
  not not_2 (not_2_out, Branch_relative);
  _16_bit_carry u_16_bit_carry_1 (
    .a(Instruction_address), .b(16'h1), .s(n16_bit_carry_1_s), .in_1(1'b0));  // open: P, G
  and and_1 (and_2_out[1], not_1_out, Branch_relative);
  and and_2 (and_2_out[0], Branch_absolute, not_2_out);
  Multiplexer #(.select(2), .width(16), .enable("false")) multiplexer_1 (
    .in0(n16_bit_carry_1_s), .in1(Branch_value), .in2(n16_bit_carry_2_s), .out(multiplexer_1_out),
    .sel(and_2_out));  // open: in3
  _16_bit_carry u_16_bit_carry_2 (
    .a(n16_bit_carry_1_s), .b(Branch_value), .s(n16_bit_carry_2_s), .in_1(1'b0));  // open: P, G
  _16_bit_register u_16_bit_register_1 (
    .D(multiplexer_1_out), .out_5(Instruction_address), .reset(Reset), .Clock(Clock));  // open: write

  // Notes on the sheet:
  //   This circuit also double checks that branch absolute and branch relative cannot be 1 at the same time.
  //   In that case, the program counter will assume human arror and will use the relative branch.
  //   When both absolute as relative are 0, the circuit program will count normally.
endmodule

module _16_bit_file_register_modified (
  input  [3:0] rd,
  input  [15:0] data,
  input  [3:0] rs,
  input  write,
  input  Clock,
  input  reset,
  input  [3:0] rt,
  output [15:0] r0,
  output [15:0] r4,
  output [15:0] r8,
  output [15:0] r12,
  output [15:0] r1,
  output [15:0] r5,
  output [15:0] r9,
  output [15:0] r13,
  output [15:0] r2,
  output [15:0] r6,
  output [15:0] r10,
  output [15:0] r14,
  output [15:0] r3,
  output [15:0] r7,
  output [15:0] r11,
  output [15:0] r15,
  output [15:0] rs_output,
  output [15:0] rt_output
);

  wire and_1_out, and_2_out, and_3_out, and_4_out, and_5_out, and_6_out, and_7_out, and_8_out, and_9_out,
       and_10_out, and_11_out, and_12_out, and_13_out, and_14_out, and_15_out, decoder_1_out1,
       decoder_1_out2, decoder_1_out3, decoder_1_out4, decoder_1_out5, decoder_1_out6, decoder_1_out7,
       decoder_1_out8, decoder_1_out9, decoder_1_out10, decoder_1_out11, decoder_1_out12, decoder_1_out13,
       decoder_1_out14, decoder_1_out15;

  Decoder #(.select(4), .enable("false")) decoder_1 (
    .out1(decoder_1_out1), .out2(decoder_1_out2), .out3(decoder_1_out3), .out4(decoder_1_out4),
    .out5(decoder_1_out5), .out6(decoder_1_out6), .out7(decoder_1_out7), .out8(decoder_1_out8),
    .out9(decoder_1_out9), .out10(decoder_1_out10), .out11(decoder_1_out11), .out12(decoder_1_out12),
    .out13(decoder_1_out13), .out14(decoder_1_out14), .out15(decoder_1_out15), .sel(rd));  // open: out0
  and and_1 (and_1_out, write, decoder_1_out1);
  and and_2 (and_2_out, write, decoder_1_out2);
  and and_3 (and_3_out, write, decoder_1_out3);
  _16_bit_register u_16_bit_register_1 (.D({16{1'b0}}), .out_5(r0), .reset(reset), .Clock(Clock));  // open: write
  _16_bit_register u_16_bit_register_2 (.write(and_1_out), .D(data), .out_5(r1), .reset(reset), .Clock(Clock));
  _16_bit_register u_16_bit_register_3 (.write(and_2_out), .D(data), .out_5(r2), .reset(reset), .Clock(Clock));
  _16_bit_register u_16_bit_register_4 (.write(and_3_out), .D(data), .out_5(r3), .reset(reset), .Clock(Clock));
  and and_4 (and_4_out, write, decoder_1_out4);
  and and_5 (and_5_out, write, decoder_1_out5);
  and and_6 (and_6_out, write, decoder_1_out6);
  and and_7 (and_7_out, write, decoder_1_out7);
  _16_bit_register u_16_bit_register_5 (.write(and_4_out), .D(data), .out_5(r4), .reset(reset), .Clock(Clock));
  _16_bit_register u_16_bit_register_6 (.write(and_5_out), .D(data), .out_5(r5), .reset(reset), .Clock(Clock));
  _16_bit_register u_16_bit_register_7 (.write(and_6_out), .D(data), .out_5(r6), .reset(reset), .Clock(Clock));
  _16_bit_register u_16_bit_register_8 (.write(and_7_out), .D(data), .out_5(r7), .reset(reset), .Clock(Clock));
  and and_8 (and_8_out, write, decoder_1_out8);
  and and_9 (and_9_out, write, decoder_1_out9);
  and and_10 (and_10_out, write, decoder_1_out10);
  and and_11 (and_11_out, write, decoder_1_out11);
  _16_bit_register u_16_bit_register_9 (.write(and_8_out), .D(data), .out_5(r8), .reset(reset), .Clock(Clock));
  _16_bit_register u_16_bit_register_10 (.write(and_9_out), .D(data), .out_5(r9), .reset(reset), .Clock(Clock));
  _16_bit_register u_16_bit_register_11 (.write(and_10_out), .D(data), .out_5(r10), .reset(reset), .Clock(Clock));
  _16_bit_register u_16_bit_register_12 (.write(and_11_out), .D(data), .out_5(r11), .reset(reset), .Clock(Clock));
  and and_12 (and_12_out, write, decoder_1_out12);
  and and_13 (and_13_out, write, decoder_1_out13);
  and and_14 (and_14_out, write, decoder_1_out14);
  and and_15 (and_15_out, write, decoder_1_out15);
  _16_bit_register u_16_bit_register_13 (.write(and_12_out), .D(data), .out_5(r12), .reset(reset), .Clock(Clock));
  _16_bit_register u_16_bit_register_14 (.write(and_13_out), .D(data), .out_5(r13), .reset(reset), .Clock(Clock));
  _16_bit_register u_16_bit_register_15 (.write(and_14_out), .D(data), .out_5(r14), .reset(reset), .Clock(Clock));
  _16_bit_register u_16_bit_register_16 (.write(and_15_out), .D(data), .out_5(r15), .reset(reset), .Clock(Clock));
  Multiplexer #(.select(4), .width(16), .enable("false")) multiplexer_1 (
    .in0(r0), .in1(r1), .in2(r2), .in3(r3), .in4(r4), .in5(r5), .in6(r6), .in7(r7), .in8(r8), .in9(r9),
    .in10(r10), .in11(r11), .in12(r12), .in13(r13), .in14(r14), .in15(r15), .out(rs_output), .sel(rs));
  Multiplexer #(.select(4), .width(16), .enable("false")) multiplexer_2 (
    .in0(r0), .in1(r1), .in2(r2), .in3(r3), .in4(r4), .in5(r5), .in6(r6), .in7(r7), .in8(r8), .in9(r9),
    .in10(r10), .in11(r11), .in12(r12), .in13(r13), .in14(r14), .in15(r15), .out(rt_output), .sel(rt));
endmodule

module Control (
  input  [3:0] in_1,
  output Unary_ALU_op,
  output ALU_op,
  output lw,
  output sw
);

  wire and_1_out, and_3_out, and_4_out, and_5_out, and_6_out, and_7_out, and_8_out, and_9_out, and_10_out,
       not_1_out, not_2_out, not_3_out, not_4_out;

  not not_1 (not_1_out, in_1[0]);
  not not_2 (not_2_out, in_1[1]);
  not not_3 (not_3_out, in_1[3]);
  not not_4 (not_4_out, in_1[2]);
  and and_1 (and_1_out, not_1_out, not_2_out, not_4_out, not_3_out);
  and and_2 (Unary_ALU_op, in_1[0], not_2_out, not_4_out, not_3_out);
  and and_3 (and_3_out, not_1_out, in_1[1], not_4_out, not_3_out);
  and and_4 (and_4_out, in_1[0], in_1[1], not_4_out, not_3_out);
  and and_5 (and_5_out, not_1_out, not_2_out, in_1[2], not_3_out);
  and and_6 (and_6_out, in_1[0], not_2_out, in_1[2], not_3_out);
  and and_7 (and_7_out, not_1_out, in_1[1], in_1[2], not_3_out);
  and and_8 (and_8_out, in_1[0], in_1[1], in_1[2], not_3_out);
  and and_9 (and_9_out, not_1_out, not_2_out, not_4_out, in_1[3]);
  and and_10 (and_10_out, in_1[0], not_2_out, not_4_out, in_1[3]);
  and and_11 (lw, not_1_out, in_1[1], not_4_out, in_1[3]);
  and and_12 (sw, in_1[0], in_1[1], not_4_out, in_1[3]);
  or or_1 (ALU_op, and_1_out, and_3_out, and_4_out, and_5_out, and_10_out, and_6_out, and_7_out, and_8_out, and_9_out);
endmodule

module ALU_control (
  input  [3:0] _0_3,
  input  [3:0] _12_15,
  input  Unary_alu_op,
  input  Alu_op,
  input  sw,
  input  lw,
  input  ori,
  input  brnz,
  output [3:0] out_9
);

  wire [0:0] or_1_out;
  wire [3:0] multiplexer_1_out, multiplexer_2_out, multiplexer_3_out;

  Multiplexer #(.width(4), .enable("false")) multiplexer_1 (
    .in0(4'b1111), .in1(_12_15), .out(multiplexer_1_out), .sel(Alu_op));
  Multiplexer #(.width(4), .enable("false")) multiplexer_2 (
    .in0(multiplexer_1_out), .in1(_0_3), .out(multiplexer_2_out), .sel(Unary_alu_op));
  or or_1 (or_1_out[0], sw, lw);
  Multiplexer #(.select(2), .width(4), .enable("false")) multiplexer_3 (
    .in0(multiplexer_2_out), .in1(4'b0100), .in2(4'b0011), .out(multiplexer_3_out), .sel({ori, or_1_out[0]}));  // open: in3
  Multiplexer #(.width(4), .enable("false")) multiplexer_4 (
    .in0(multiplexer_3_out), .in1(4'b1001), .out(out_9), .sel(brnz));

  // Notes on the sheet:
  //   ALU control
endmodule

module Control_unit___16_bit (
  input  [15:0] in_1,
  output [15:0] Bit_extend,
  output [3:0] rs,
  output [3:0] rt,
  output [3:0] rd,
  output Write_Disable,
  output lw,
  output sw,
  output brnz,
  output ALU_input_selector,
  output [3:0] ALU_op_code,
  output Exception_trower,
  output imm,
  output jump,
  output jal,
  output jr
);

  wire and_1_out, and_2_out, and_3_out, and_4_out, and_5_out, and_6_out, and_7_out, and_8_out, and_9_out,
       and_10_out, and_13_out, and_19_out, and_20_out, and_21_out, and_22_out, and_23_out, and_24_out,
       and_25_out, and_26_out, and_27_out, and_28_out, and_29_out, and_30_out, and_31_out, and_32_out,
       and_33_out, comparator_1_eq, comparator_2_eq, not_1_out, not_2_out, not_3_out, not_4_out, not_5_out,
       not_6_out, not_7_out, not_8_out, not_9_out, not_10_out, or_1_out, or_2_out, or_3_out, or_4_out,
       or_7_out, or_8_out, or_9_out, or_10_out, or_11_out, xor_1_out;
  wire [1:0] bitselector_1_out;
  wire [15:0] bit_extender_1_out, bit_extender_2_out, bit_extender_3_out, bit_extender_4_out,
       bit_extender_5_out, jump_addr, multiplexer_1_out, multiplexer_4_out, multiplexer_5_out, shifter_1_out;

  not not_1 (not_1_out, in_1[12]);
  not not_2 (not_2_out, in_1[13]);
  not not_3 (not_3_out, in_1[15]);
  not not_4 (not_4_out, in_1[14]);
  and and_1 (and_1_out, not_1_out, not_2_out, not_4_out, not_3_out);
  and and_2 (and_2_out, in_1[12], not_2_out, not_4_out, not_3_out);
  and and_3 (and_3_out, not_1_out, in_1[13], not_4_out, not_3_out);
  and and_4 (and_4_out, in_1[12], in_1[13], not_4_out, not_3_out);
  and and_5 (and_5_out, not_1_out, not_2_out, in_1[14], not_3_out);
  and and_6 (and_6_out, in_1[12], not_2_out, not_4_out, in_1[15]);
  and and_7 (and_7_out, in_1[12], not_2_out, in_1[14], not_3_out);
  and and_8 (and_8_out, not_1_out, in_1[13], in_1[14], not_3_out);
  and and_9 (and_9_out, in_1[12], in_1[13], in_1[14], not_3_out);
  and and_10 (and_10_out, not_1_out, not_2_out, not_4_out, in_1[15]);
  and and_11 (lw, not_1_out, in_1[13], not_4_out, in_1[15]);
  and and_12 (sw, in_1[12], in_1[13], not_4_out, in_1[15]);
  and and_13 (and_13_out, in_1[15], in_1[14], not_2_out, not_1_out);
  and and_14 (imm, in_1[15], in_1[14], not_2_out, in_1[12]);
  and and_15 (brnz, in_1[15], in_1[14], in_1[13], not_1_out);
  and and_16 (jump, in_1[15], in_1[14], in_1[13], in_1[12]);
  assign bit_extender_1_out = {{12{in_1[3]}}, in_1[3:0]};  // Bit_Extender bit_extender_1
  assign bit_extender_2_out = {{8{1'b0}}, in_1[7:0]};  // Bit_Extender bit_extender_2
  Multiplexer #(.width(16), .enable("false")) multiplexer_1 (
    .in0(bit_extender_2_out), .in1(bit_extender_3_out), .out(multiplexer_1_out), .sel(brnz));
  assign bit_extender_3_out = {{8{in_1[7]}}, in_1[7:0]};  // Bit_Extender bit_extender_3
  Multiplexer #(.width(4), .enable("false")) multiplexer_2 (.in0(in_1[3:0]), .in1(in_1[11:8]), .out(rt), .sel(sw));
  or or_1 (or_1_out, and_1_out, and_3_out, and_4_out, and_5_out, and_6_out, and_7_out, and_8_out, and_9_out, and_10_out);
  xor xor_1 (xor_1_out, bitselector_1_out[0], bitselector_1_out[1]);
  BitSelector #(.width(4), .group(2)) bitselector_1 (.in(in_1[3:0]), .out(bitselector_1_out), .sel(1'b1));
  assign bit_extender_4_out = {{8{1'b0}}, in_1[11:4]};  // Bit_Extender bit_extender_4
  assign bit_extender_5_out = {{12{in_1[7]}}, in_1[7:4]};  // Bit_Extender bit_extender_5
  Shifter #(.width(16)) shifter_1 (.in(multiplexer_1_out), .\dist (4'b1000), .out(shifter_1_out));
  or or_2 (or_2_out, and_2_out, jump);
  and and_17 (jr, jump, xor_1_out);
  Multiplexer #(.width(16), .enable("false")) multiplexer_3 (
    .in0(bit_extender_4_out), .in1(bit_extender_5_out), .out(jump_addr), .sel(xor_1_out));
  Multiplexer #(.width(16), .enable("false")) multiplexer_4 (
    .in0(multiplexer_1_out), .in1(shifter_1_out), .out(multiplexer_4_out), .sel(imm));
  or or_3 (or_3_out, jump, or_4_out);
  or or_4 (or_4_out, and_13_out, imm, brnz);
  and and_18 (jal, jump, in_1[0], in_1[1], in_1[2], in_1[3]);
  Multiplexer #(.width(16), .enable("false")) multiplexer_5 (
    .in0(bit_extender_1_out), .in1(multiplexer_4_out), .out(multiplexer_5_out), .sel(or_4_out));
  Multiplexer #(.width(4), .enable("false")) multiplexer_6 (
    .in0(in_1[7:4]), .in1(in_1[11:8]), .out(rs), .sel(or_3_out));
  and and_19 (and_19_out, ~jal, jump);  // AND_Gate
  or or_5 (Write_Disable, and_19_out, brnz);
  or or_6 (ALU_input_selector, sw, or_4_out, lw, jump);
  Multiplexer #(.width(16), .enable("false")) multiplexer_7 (
    .in0(multiplexer_5_out), .in1(jump_addr), .out(Bit_extend), .sel(jump));
  Multiplexer #(.width(4), .enable("false")) multiplexer_8 (.in0(in_1[11:8]), .in1(4'b1111), .out(rd), .sel(jal));
  ALU_control alu_control_1 (
    ._0_3(in_1[3:0]), ._12_15(in_1[15:12]), .Unary_alu_op(or_2_out), .Alu_op(or_1_out), .sw(sw), .lw(lw),
    .out_9(ALU_op_code), .ori(and_13_out), .brnz(brnz));
  not not_5 (not_5_out, or_7_out);
  or or_7 (or_7_out, or_1_out, brnz, or_4_out, and_13_out, sw, lw, jump, brnz);
  not not_6 (not_6_out, or_8_out);
  or or_8 (or_8_out, or_2_out, or_1_out, brnz, or_4_out, and_13_out, sw, lw, brnz);
  and and_20 (and_20_out, or_2_out, not_5_out);
  Comparator #(.width(4)) comparator_1 (.a(in_1[3:0]), .b(4'b0000), .eq(comparator_1_eq));  // open: gt, lt
  Comparator #(.width(4)) comparator_2 (.a(in_1[7:4]), .b(4'b0000), .eq(comparator_2_eq));  // open: gt, lt
  not not_7 (not_7_out, in_1[0]);
  not not_8 (not_8_out, in_1[1]);
  not not_9 (not_9_out, in_1[2]);
  not not_10 (not_10_out, in_1[3]);
  and and_21 (and_21_out, in_1[0], not_8_out, not_9_out, not_10_out);
  and and_22 (and_22_out, jump, not_6_out);
  and and_23 (and_23_out, not_7_out, in_1[1], not_9_out, in_1[3]);
  and and_24 (and_24_out, in_1[0], in_1[1], not_9_out, in_1[3]);
  or or_9 (or_9_out, ~comparator_1_eq, ~comparator_2_eq);  // OR_Gate
  and and_25 (and_25_out, not_7_out, not_8_out, in_1[2], in_1[3]);
  and and_26 (and_26_out, or_9_out, and_1_out);
  and and_27 (and_27_out, in_1[0], not_8_out, in_1[2], in_1[3]);
  and and_28 (and_28_out, not_7_out, in_1[1], in_1[2], in_1[3]);
  and and_29 (and_29_out, not_7_out, not_8_out, in_1[2], not_10_out);
  and and_30 (and_30_out, in_1[0], in_1[1], in_1[2], in_1[3]);
  and and_31 (and_31_out, not_7_out, not_8_out, not_9_out, not_10_out);
  or or_10 (or_10_out, and_30_out, and_28_out, and_27_out, and_25_out, and_24_out, and_23_out, and_21_out);
  or or_11 (or_11_out, and_30_out, and_29_out, and_31_out);
  and and_32 (and_32_out, and_20_out, ~or_10_out);  // AND_Gate
  and and_33 (and_33_out, and_22_out, or_11_out);
  or or_12 (Exception_trower, and_32_out, and_26_out, and_33_out);

  // Other names for the same wires on the sheet: rt_t[3:0] = in_1[3:0]; rs_t[3:0] = in_1[7:4]; rd_t[3:0] = in_1[11:8];
  //   j = jr; upper = imm

  // Notes on the sheet:
  //   13
  //   14
  //   12
  //   15
  //   Part for deciding which operation we are doing
endmodule

module Test (
  input  abs,
  input  rel,
  output [1:0] out
);

  wire not_1_out, not_2_out;

  not not_1 (not_1_out, abs);
  not not_2 (not_2_out, rel);
  and and_1 (out[1], not_1_out, rel);
  and and_2 (out[0], abs, not_2_out);
endmodule
