// Logisim project Memory.circ as structural Verilog
module D_flip_flop_falling_edge (
  input  in_1,
  input  in_2,
  output out_3,
  output out_4
);

  wire clock_1_out;

  Clock clock_1 (.out(clock_1_out));
  D_Flip_Flop #(.trigger("falling")) d_ff_1 (
    .clk(clock_1_out), .D(in_1), .Q(out_3), .Qn(out_4), .en(in_2));  // open: preset, reset
endmodule

module _16_bit_register (
  input  Clock,
  input  write,
  input  reset,
  input  [15:0] D,
  output [15:0] out_5
);

  D_Flip_Flop #(.trigger("falling")) d_ff_1 (
    .clk(Clock), .D(D[0]), .Q(out_5[0]), .en(write), .reset(reset));  // open: Qn, preset
  D_Flip_Flop #(.trigger("falling")) d_ff_2 (
    .clk(Clock), .D(D[1]), .Q(out_5[1]), .en(write), .reset(reset));  // open: Qn, preset
  D_Flip_Flop #(.trigger("falling")) d_ff_3 (
    .clk(Clock), .D(D[2]), .Q(out_5[2]), .en(write), .reset(reset));  // open: Qn, preset
  D_Flip_Flop #(.trigger("falling")) d_ff_4 (
    .clk(Clock), .D(D[3]), .Q(out_5[3]), .en(write), .reset(reset));  // open: Qn, preset
  D_Flip_Flop #(.trigger("falling")) d_ff_5 (
    .clk(Clock), .D(D[4]), .Q(out_5[4]), .en(write), .reset(reset));  // open: Qn, preset
  D_Flip_Flop #(.trigger("falling")) d_ff_6 (
    .clk(Clock), .D(D[5]), .Q(out_5[5]), .en(write), .reset(reset));  // open: Qn, preset
  D_Flip_Flop #(.trigger("falling")) d_ff_7 (
    .clk(Clock), .D(D[6]), .Q(out_5[6]), .en(write), .reset(reset));  // open: Qn, preset
  D_Flip_Flop #(.trigger("falling")) d_ff_8 (
    .clk(Clock), .D(D[7]), .Q(out_5[7]), .en(write), .reset(reset));  // open: Qn, preset
  D_Flip_Flop #(.trigger("falling")) d_ff_9 (
    .clk(Clock), .D(D[8]), .Q(out_5[8]), .en(write), .reset(reset));  // open: Qn, preset
  D_Flip_Flop #(.trigger("falling")) d_ff_10 (
    .clk(Clock), .D(D[9]), .Q(out_5[9]), .en(write), .reset(reset));  // open: Qn, preset
  D_Flip_Flop #(.trigger("falling")) d_ff_11 (
    .clk(Clock), .D(D[10]), .Q(out_5[10]), .en(write), .reset(reset));  // open: Qn, preset
  D_Flip_Flop #(.trigger("falling")) d_ff_12 (
    .clk(Clock), .D(D[11]), .Q(out_5[11]), .en(write), .reset(reset));  // open: Qn, preset
  D_Flip_Flop #(.trigger("falling")) d_ff_13 (
    .clk(Clock), .D(D[12]), .Q(out_5[12]), .en(write), .reset(reset));  // open: Qn, preset
  D_Flip_Flop #(.trigger("falling")) d_ff_14 (
    .clk(Clock), .D(D[13]), .Q(out_5[13]), .en(write), .reset(reset));  // open: Qn, preset
  D_Flip_Flop #(.trigger("falling")) d_ff_15 (
    .clk(Clock), .D(D[14]), .Q(out_5[14]), .en(write), .reset(reset));  // open: Qn, preset
  D_Flip_Flop #(.trigger("falling")) d_ff_16 (
    .clk(Clock), .D(D[15]), .Q(out_5[15]), .en(write), .reset(reset));  // open: Qn, preset

  // Notes on the sheet:
  //   Change 'clock' back to the clock in the wiring library if you want to test this circuit.
endmodule

module Register_file_edit (
  input  [3:0] rd,
  input  [15:0] data,
  input  [3:0] rs,
  input  write,
  input  Clock,
  input  reset,
  input  [3:0] rt,
  output [15:0] rs_output,
  output [15:0] rt_output
);

  wire and_1_out, and_2_out, and_3_out, and_4_out, and_5_out, and_6_out, and_7_out, and_8_out, and_9_out,
       and_10_out, and_11_out, and_12_out, and_13_out, and_14_out, and_15_out, decoder_1_out1,
       decoder_1_out2, decoder_1_out3, decoder_1_out4, decoder_1_out5, decoder_1_out6, decoder_1_out7,
       decoder_1_out8, decoder_1_out9, decoder_1_out10, decoder_1_out11, decoder_1_out12, decoder_1_out13,
       decoder_1_out14, decoder_1_out15;
  wire [15:0] n16_bit_register_1_out_5, n16_bit_register_2_out_5, n16_bit_register_3_out_5,
       n16_bit_register_4_out_5, n16_bit_register_5_out_5, n16_bit_register_6_out_5,
       n16_bit_register_7_out_5, n16_bit_register_8_out_5, n16_bit_register_9_out_5,
       n16_bit_register_10_out_5, n16_bit_register_11_out_5, n16_bit_register_12_out_5,
       n16_bit_register_13_out_5, n16_bit_register_14_out_5, n16_bit_register_15_out_5,
       n16_bit_register_16_out_5;

  Decoder #(.select(4)) decoder_1 (
    .out1(decoder_1_out1), .out2(decoder_1_out2), .out3(decoder_1_out3), .out4(decoder_1_out4),
    .out5(decoder_1_out5), .out6(decoder_1_out6), .out7(decoder_1_out7), .out8(decoder_1_out8),
    .out9(decoder_1_out9), .out10(decoder_1_out10), .out11(decoder_1_out11), .out12(decoder_1_out12),
    .out13(decoder_1_out13), .out14(decoder_1_out14), .out15(decoder_1_out15), .sel(rd));  // open: out0, en
  and and_1 (and_1_out, write, decoder_1_out1);
  and and_2 (and_2_out, write, decoder_1_out2);
  and and_3 (and_3_out, write, decoder_1_out3);
  _16_bit_register u_16_bit_register_1 (
    .D({16{1'b0}}), .out_5(n16_bit_register_1_out_5), .reset(reset), .Clock(Clock));  // open: write
  _16_bit_register u_16_bit_register_2 (
    .write(and_1_out), .D(data), .out_5(n16_bit_register_2_out_5), .reset(reset), .Clock(Clock));
  _16_bit_register u_16_bit_register_3 (
    .write(and_2_out), .D(data), .out_5(n16_bit_register_3_out_5), .reset(reset), .Clock(Clock));
  _16_bit_register u_16_bit_register_4 (
    .write(and_3_out), .D(data), .out_5(n16_bit_register_4_out_5), .reset(reset), .Clock(Clock));
  and and_4 (and_4_out, write, decoder_1_out4);
  and and_5 (and_5_out, write, decoder_1_out5);
  and and_6 (and_6_out, write, decoder_1_out6);
  and and_7 (and_7_out, write, decoder_1_out7);
  _16_bit_register u_16_bit_register_5 (
    .write(and_4_out), .D(data), .out_5(n16_bit_register_5_out_5), .reset(reset), .Clock(Clock));
  _16_bit_register u_16_bit_register_6 (
    .write(and_5_out), .D(data), .out_5(n16_bit_register_6_out_5), .reset(reset), .Clock(Clock));
  _16_bit_register u_16_bit_register_7 (
    .write(and_6_out), .D(data), .out_5(n16_bit_register_7_out_5), .reset(reset), .Clock(Clock));
  _16_bit_register u_16_bit_register_8 (
    .write(and_7_out), .D(data), .out_5(n16_bit_register_8_out_5), .reset(reset), .Clock(Clock));
  and and_8 (and_8_out, write, decoder_1_out8);
  and and_9 (and_9_out, write, decoder_1_out9);
  and and_10 (and_10_out, write, decoder_1_out10);
  and and_11 (and_11_out, write, decoder_1_out11);
  _16_bit_register u_16_bit_register_9 (
    .write(and_8_out), .D(data), .out_5(n16_bit_register_9_out_5), .reset(reset), .Clock(Clock));
  _16_bit_register u_16_bit_register_10 (
    .write(and_9_out), .D(data), .out_5(n16_bit_register_10_out_5), .reset(reset), .Clock(Clock));
  _16_bit_register u_16_bit_register_11 (
    .write(and_10_out), .D(data), .out_5(n16_bit_register_11_out_5), .reset(reset), .Clock(Clock));
  _16_bit_register u_16_bit_register_12 (
    .write(and_11_out), .D(data), .out_5(n16_bit_register_12_out_5), .reset(reset), .Clock(Clock));
  and and_12 (and_12_out, write, decoder_1_out12);
  and and_13 (and_13_out, write, decoder_1_out13);
  and and_14 (and_14_out, write, decoder_1_out14);
  and and_15 (and_15_out, write, decoder_1_out15);
  _16_bit_register u_16_bit_register_13 (
    .write(and_12_out), .D(data), .out_5(n16_bit_register_13_out_5), .reset(reset), .Clock(Clock));
  _16_bit_register u_16_bit_register_14 (
    .write(and_13_out), .D(data), .out_5(n16_bit_register_14_out_5), .reset(reset), .Clock(Clock));
  _16_bit_register u_16_bit_register_15 (
    .write(and_14_out), .D(data), .out_5(n16_bit_register_15_out_5), .reset(reset), .Clock(Clock));
  _16_bit_register u_16_bit_register_16 (
    .write(and_15_out), .D(data), .out_5(n16_bit_register_16_out_5), .reset(reset), .Clock(Clock));
  Multiplexer #(.select(4), .width(16), .enable("false")) multiplexer_1 (
    .in0(n16_bit_register_1_out_5), .in1(n16_bit_register_2_out_5), .in2(n16_bit_register_3_out_5),
    .in3(n16_bit_register_4_out_5), .in4(n16_bit_register_5_out_5), .in5(n16_bit_register_6_out_5),
    .in6(n16_bit_register_7_out_5), .in7(n16_bit_register_8_out_5), .in8(n16_bit_register_9_out_5),
    .in9(n16_bit_register_10_out_5), .in10(n16_bit_register_11_out_5), .in11(n16_bit_register_12_out_5),
    .in12(n16_bit_register_13_out_5), .in13(n16_bit_register_14_out_5), .in14(n16_bit_register_15_out_5),
    .in15(n16_bit_register_16_out_5), .out(rs_output), .sel(rs));
  Multiplexer #(.select(4), .width(16), .enable("false")) multiplexer_2 (
    .in0(n16_bit_register_1_out_5), .in1(n16_bit_register_2_out_5), .in2(n16_bit_register_3_out_5),
    .in3(n16_bit_register_4_out_5), .in4(n16_bit_register_5_out_5), .in5(n16_bit_register_6_out_5),
    .in6(n16_bit_register_7_out_5), .in7(n16_bit_register_8_out_5), .in8(n16_bit_register_9_out_5),
    .in9(n16_bit_register_10_out_5), .in10(n16_bit_register_11_out_5), .in11(n16_bit_register_12_out_5),
    .in12(n16_bit_register_13_out_5), .in13(n16_bit_register_14_out_5), .in14(n16_bit_register_15_out_5),
    .in15(n16_bit_register_16_out_5), .out(rt_output), .sel(rt));
endmodule

module Counter (
  input  [15:0] in_1,
  output [15:0] out_2
);

  wire comparator_1_eq, comparator_1_gt, comparator_1_lt, or_1_out;
  wire [0:0] clock_1_out;
  wire [15:0] n16_bit_carry_1_s;

  Clock clock_1 (.out(clock_1_out[0]));
  _16_bit_carry u_16_bit_carry_1 (
    .a(out_2), .b({{15{1'b0}}, clock_1_out[0]}), .s(n16_bit_carry_1_s), .in_1(1'b0));  // open: P, G
  _16_bit_register u_16_bit_register_1 (
    .write(comparator_1_lt), .D(n16_bit_carry_1_s), .out_5(out_2), .reset(or_1_out), .Clock(clock_1_out[0]));
  or or_1 (or_1_out, comparator_1_eq, comparator_1_gt);
  Comparator #(.width(16), .mode("unsigned")) comparator_1 (
    .a(out_2), .b(in_1), .gt(comparator_1_gt), .eq(comparator_1_eq), .lt(comparator_1_lt));

  // Notes on the sheet:
  //   De OR-gate tussen > en = moet op zich niet, maar is een veiligheid voor als de user de input tijdens het runnen aanpast.
  //   Er zal in dat geval een reset gebeuren.
endmodule

module _16_bit_carry (
  input  in_1,
  input  [15:0] a,
  input  [15:0] b,
  output [15:0] s,
  output P,
  output G
);

  wire and_1_out, and_2_out, and_3_out, and_4_out, and_5_out, and_6_out, n4_bit_adder_1_g0,
       n4_bit_adder_1_p0, n4_bit_adder_2_g0, n4_bit_adder_2_p0, n4_bit_adder_3_g0, n4_bit_adder_3_p0,
       or_1_out, or_2_out, or_3_out;

  and and_1 (and_1_out, and_5_out, n4_bit_adder_3_p0);
  and and_2 (and_2_out, and_4_out, n4_bit_adder_3_p0);
  _4_bit_adder u_4_bit_adder_1 (
    .a(a[3:0]), .b(b[3:0]), .CarryIn(in_1), .P0(n4_bit_adder_1_p0), .G0(n4_bit_adder_1_g0), .S(s[3:0]));
  and and_3 (and_3_out, in_1, n4_bit_adder_1_p0);
  or or_1 (or_1_out, and_3_out, n4_bit_adder_1_g0);
  _4_bit_adder u_4_bit_adder_2 (
    .a(a[7:4]), .b(b[7:4]), .CarryIn(or_1_out), .P0(n4_bit_adder_2_p0), .G0(n4_bit_adder_2_g0), .S(s[7:4]));
  and and_4 (and_4_out, and_3_out, n4_bit_adder_2_p0);
  and and_5 (and_5_out, n4_bit_adder_1_g0, n4_bit_adder_2_p0);
  or or_2 (or_2_out, and_4_out, and_5_out, n4_bit_adder_2_g0);
  _4_bit_adder u_4_bit_adder_3 (
    .a(a[11:8]), .b(b[11:8]), .CarryIn(or_2_out), .P0(n4_bit_adder_3_p0), .G0(n4_bit_adder_3_g0), .S(s[11:8]));
  and and_6 (and_6_out, n4_bit_adder_2_g0, n4_bit_adder_3_p0);
  or or_3 (or_3_out, and_2_out, and_1_out, and_6_out, n4_bit_adder_3_g0);
  _4_bit_adder u_4_bit_adder_4 (.a(a[15:12]), .b(b[15:12]), .CarryIn(or_3_out), .P0(P), .G0(G), .S(s[15:12]));
endmodule

module _4_bit_adder (
  input  CarryIn,
  input  [3:0] a,
  input  [3:0] b,
  output [3:0] S,
  output P0,
  output G0
);

  wire and_1_out, and_2_out, and_3_out, and_4_out, and_5_out, and_6_out, and_7_out, and_8_out, and_9_out,
       and_10_out, and_11_out, and_12_out, and_14_out, and_15_out, and_16_out, and_17_out, and_18_out,
       and_19_out, and_20_out, and_21_out, and_22_out, and_23_out, and_24_out, and_25_out, and_26_out,
       and_27_out, not_1_out, not_2_out, not_3_out, not_4_out, not_5_out, not_6_out, not_7_out, not_8_out,
       not_9_out, not_10_out, not_11_out, not_12_out, or_1_out, or_2_out, or_3_out, or_4_out, or_7_out,
       or_8_out, or_9_out;

  or or_1 (or_1_out, and_1_out, and_2_out);
  not not_1 (not_1_out, a[0]);
  not not_2 (not_2_out, b[0]);
  not not_3 (not_3_out, CarryIn);
  and and_1 (and_1_out, a[0], b[0]);
  and and_2 (and_2_out, or_3_out, CarryIn);
  not not_4 (not_4_out, a[1]);
  not not_5 (not_5_out, b[1]);
  not not_6 (not_6_out, or_1_out);
  and and_3 (and_3_out, a[1], b[1]);
  and and_4 (and_4_out, or_1_out, or_4_out);
  or or_2 (or_2_out, and_3_out, and_4_out);
  or or_3 (or_3_out, a[0], b[0]);
  or or_4 (or_4_out, a[1], b[1]);
  and and_5 (and_5_out, not_1_out, b[0], not_3_out);
  and and_6 (and_6_out, a[0], not_2_out, not_3_out);
  and and_7 (and_7_out, not_4_out, b[1], not_6_out);
  and and_8 (and_8_out, a[1], not_5_out, not_6_out);
  and and_9 (and_9_out, a[0], b[0], CarryIn);
  and and_10 (and_10_out, not_1_out, not_2_out, CarryIn);
  and and_11 (and_11_out, not_4_out, not_5_out, or_1_out);
  and and_12 (and_12_out, a[1], b[1], or_1_out);
  or or_5 (S[0], and_9_out, and_10_out, and_5_out, and_6_out);
  or or_6 (S[1], and_12_out, and_11_out, and_7_out, and_8_out);
  or or_7 (or_7_out, and_14_out, and_15_out);
  and and_13 (P0, or_3_out, or_4_out, or_8_out, or_9_out);
  not not_7 (not_7_out, a[2]);
  not not_8 (not_8_out, b[2]);
  not not_9 (not_9_out, or_2_out);
  and and_14 (and_14_out, a[2], b[2]);
  and and_15 (and_15_out, or_8_out, or_2_out);
  not not_10 (not_10_out, b[3]);
  not not_11 (not_11_out, a[3]);
  not not_12 (not_12_out, or_7_out);
  and and_16 (and_16_out, b[3], a[3]);
  and and_17 (and_17_out, or_9_out, and_14_out);
  or or_8 (or_8_out, a[2], b[2]);
  or or_9 (or_9_out, b[3], a[3]);
  and and_18 (and_18_out, or_9_out, or_8_out, and_3_out);
  or or_10 (G0, and_16_out, and_17_out, and_18_out, and_23_out);
  and and_19 (and_19_out, a[2], not_8_out, not_9_out);
  and and_20 (and_20_out, not_7_out, b[2], not_9_out);
  and and_21 (and_21_out, not_10_out, a[3], not_12_out);
  and and_22 (and_22_out, b[3], not_11_out, not_12_out);
  and and_23 (and_23_out, or_9_out, or_8_out, or_4_out, and_1_out);
  and and_24 (and_24_out, not_7_out, not_8_out, or_2_out);
  and and_25 (and_25_out, a[2], b[2], or_2_out);
  and and_26 (and_26_out, b[3], a[3], or_7_out);
  and and_27 (and_27_out, not_10_out, not_11_out, or_7_out);
  or or_11 (S[2], and_25_out, and_24_out, and_20_out, and_19_out);
  or or_12 (S[3], and_26_out, and_27_out, and_21_out, and_22_out);
endmodule

module Traffic_lights_system (
  input  Write,
  input  Reset,
  input  [15:0] in_3,
  input  [15:0] in_4,
  input  [15:0] in_5
);

  wire button_1_out, Clock_out, comparator_1_gt, comparator_2_gt, not_1_out, not_2_out,
       traffic_lights_system_next_state_1_s0_2, traffic_lights_system_next_state_1_s1_2,
       traffic_lights_system_next_state_1_s2_2, traffic_lights_system_next_state_2_s0_2,
       traffic_lights_system_next_state_2_s1_2, traffic_lights_system_next_state_2_s2_2;
  wire [2:0] d_ff_2_q, d_ff_5_q;
  wire [15:0] counter_1_out_2, counter_2_out_2, multiplexer_1_out, multiplexer_2_out,
       n16_bit_register_1_out_5, n16_bit_register_2_out_5, n16_bit_register_3_out_5;

  D_Flip_Flop #(.trigger("falling")) d_ff_1 (
    .clk(Clock_out), .D(traffic_lights_system_next_state_1_s0_2), .Q(d_ff_2_q[2]), .en(not_2_out));  // open: Qn, preset, reset
  Button button_1 (.out(button_1_out));
  D_Flip_Flop #(.trigger("falling")) d_ff_2 (
    .clk(Clock_out), .D(traffic_lights_system_next_state_1_s1_2), .Q(d_ff_2_q[0]), .en(not_2_out));  // open: Qn, preset, reset
  Clock Clock (.out(Clock_out));
  D_Flip_Flop #(.trigger("falling")) d_ff_3 (
    .clk(Clock_out), .D(traffic_lights_system_next_state_1_s2_2), .Q(d_ff_2_q[1]), .en(not_2_out));  // open: Qn, preset, reset
  _16_bit_register u_16_bit_register_1 (
    .write(Write), .D(in_3), .out_5(n16_bit_register_1_out_5), .reset(Reset), .Clock(Clock_out));
  _16_bit_register u_16_bit_register_2 (
    .write(Write), .D(in_4), .out_5(n16_bit_register_2_out_5), .reset(Reset), .Clock(Clock_out));
  _16_bit_register u_16_bit_register_3 (
    .write(Write), .D(in_5), .out_5(n16_bit_register_3_out_5), .reset(Reset), .Clock(Clock_out));
  D_Flip_Flop #(.trigger("falling")) d_ff_4 (
    .clk(Clock_out), .D(traffic_lights_system_next_state_2_s0_2), .Q(d_ff_5_q[2]), .en(not_1_out));  // open: Qn, preset, reset
  Multiplexer #(.select(3), .width(16), .enable("false")) multiplexer_1 (
    .in0({16{1'b0}}), .in1(n16_bit_register_1_out_5), .in2(n16_bit_register_2_out_5),
    .in4(n16_bit_register_3_out_5), .out(multiplexer_1_out), .sel(d_ff_5_q));  // open: in3, in5, in6, in7
  Multiplexer #(.select(3), .width(16), .enable("false")) multiplexer_2 (
    .in0({16{1'b0}}), .in1(n16_bit_register_3_out_5), .in2(n16_bit_register_2_out_5),
    .in4(n16_bit_register_1_out_5), .out(multiplexer_2_out), .sel(d_ff_2_q));  // open: in3, in5, in6, in7
  D_Flip_Flop #(.trigger("falling")) d_ff_5 (
    .clk(Clock_out), .D(traffic_lights_system_next_state_2_s1_2), .Q(d_ff_5_q[0]), .en(not_1_out));  // open: Qn, preset, reset
  D_Flip_Flop #(.trigger("falling")) d_ff_6 (
    .clk(Clock_out), .D(traffic_lights_system_next_state_2_s2_2), .Q(d_ff_5_q[1]), .en(not_1_out));  // open: Qn, preset, reset
  Counter counter_1 (.in_1(multiplexer_1_out), .out_2(counter_1_out_2));
  Counter counter_2 (.in_1(multiplexer_2_out), .out_2(counter_2_out_2));
  Traffic_lights_system_next_state traffic_lights_system_next_state_1 (
    .s0(d_ff_2_q[2]), .s1(d_ff_2_q[0]), .s2(d_ff_2_q[1]), .s0_2(traffic_lights_system_next_state_1_s0_2),
    .s1_2(traffic_lights_system_next_state_1_s1_2), .s2_2(traffic_lights_system_next_state_1_s2_2),
    .in_4(button_1_out));
  Comparator #(.width(16), .mode("unsigned")) comparator_1 (
    .a(counter_1_out_2), .b({16{1'b0}}), .gt(comparator_1_gt));  // open: eq, lt
  Comparator #(.width(16), .mode("unsigned")) comparator_2 (
    .a(counter_2_out_2), .b({16{1'b0}}), .gt(comparator_2_gt));  // open: eq, lt
  not not_1 (not_1_out, comparator_1_gt);
  not not_2 (not_2_out, comparator_2_gt);
  LED led_1 (.in(d_ff_2_q[0]));
  LED led_2 (.in(d_ff_2_q[1]));
  LED led_3 (.in(d_ff_2_q[2]));
  Traffic_lights_system_next_state traffic_lights_system_next_state_2 (
    .s0(d_ff_5_q[2]), .s1(d_ff_5_q[0]), .s2(d_ff_5_q[1]), .s0_2(traffic_lights_system_next_state_2_s0_2),
    .s1_2(traffic_lights_system_next_state_2_s1_2), .s2_2(traffic_lights_system_next_state_2_s2_2),
    .in_4(button_1_out));
  LED led_4 (.in(d_ff_5_q[0]));
  LED led_5 (.in(d_ff_5_q[1]));
  LED led_6 (.in(d_ff_5_q[2]));

  // Notes on the sheet:
  //   Hold button for one clock cycle to start
  //   Traffic light 2
  //   Traffic light 1
endmodule

module Traffic_lights_system_next_state (
  input  s0,
  input  s1,
  input  s2,
  input  in_4,
  output s1_2,
  output s2_2,
  output s0_2
);

  wire and_1_out, and_4_out, not_1_out, not_2_out, not_3_out, not_4_out;

  not not_1 (not_1_out, s0);
  not not_2 (not_2_out, s2);
  not not_3 (not_3_out, 1'b1);
  not not_4 (not_4_out, s1);
  and and_1 (and_1_out, not_1_out, not_4_out, s2, 1'b1);
  and and_2 (s1_2, s0, not_4_out, not_2_out, 1'b1);
  and and_3 (s2_2, not_1_out, s1, not_2_out, 1'b1);
  buf and_4 (and_4_out, in_4);  // AND_Gate
  or or_1 (s0_2, and_1_out, and_4_out);
endmodule
